# Fritzing sketch schematic_arduino-testboard_david (saved by Fritzing 0.8.5b)
breadboards: 1

parts:
  Bauteil1 = Arduino Board Ethernet
  Q1 = NPN-Transistor [package="TO92 [THT]"]
  LED1 = LEDs [package=led10mm]
  LED2 = LEDs [package=led10mm]
  R2 = Photocell (LDR) [package=THT]
  IR_Reciever_TSOP34836 = IR Reciever
  R3 = Resistor [tolerance=±10% resistance=150 package=THT]
  R4 = Resistor [tolerance=±5% resistance=3.3k package=THT]
  S1 = Toggle Switch [package=THT]
  R1 = Resistor [tolerance=±1% resistance=11k package=THT]
  R5 = Resistor [tolerance=±5% resistance=150 package=THT]
  LED3 = smd LED [color="Green (555nm)" package="1206 [SMD]"]
  LED3_2 = smd LED [color="Green (555nm)" package="0603 [SMD]"]

nets:
  N1: Bauteil1.D9_PWM, IR_Reciever_TSOP34836.OUT
  N2: Bauteil1.GND, LED1.C, LED2.C, S1.L2, R1.Pin_0, LED3.cathode, LED3_2.cathode
  N3: Bauteil1.A0, R2.pin_1, R1.Pin_1
  N4: Bauteil1.D3_PWM, R3.Pin_1
  N5: Bauteil1.D5_PWM, S1.COM
  N6: Bauteil1.D7, R5.Pin_0
  N7: Bauteil1.5V, R2.pin_0, IR_Reciever_TSOP34836.Vs, R4.Pin_0, S1.L1
  N8: Q1.B, R3.Pin_0
  N9: Q1.C, R4.Pin_1
  N10: LED1.A, LED2.A
  N11: R5.Pin_1, LED3.anode, LED3_2.anode

custom parts:
  IR Reciever: Basic infrared reciever
